// Logisim project AVF da AV2 - João Lucas Mota Cavalcante da Silva.circ as structural Verilog: 1 circuit, main circuit main
module main (
  input  CH0,
  input  CH1,
  input  CH2,
  input  CH3,
  input  CH4,
  input  CH5,
  input  CH6,
  input  CH7,
  input  CH8,
  input  CH9,
  output SD,
  output a,
  output SC,
  output b,
  output SB,
  output SA,
  output c,
  output d,
  output e,
  output f,
  output g
);

  wire and_1_out, and_2_out, and_3_out, and_4_out, and_5_out, and_6_out, and_7_out, and_8_out, and_9_out,
       and_10_out, and_11_out, and_12_out, and_13_out, and_14_out, and_15_out, and_16_out, not_1_out,
       not_2_out, not_3_out, not_4_out, not_5_out, not_6_out, not_7_out, not_8_out, not_9_out, not_10_out,
       not_11_out, not_12_out, not_13_out, not_14_out, not_15_out, not_16_out, not_17_out, not_18_out,
       not_19_out, not_20_out, not_21_out;

  or or_1 (SD, CH8, CH9);
  or or_2 (SC, CH4, CH5, CH6, CH7);
  or or_3 (SB, CH2, CH3, CH6, CH7);
  or or_4 (SA, CH1, CH3, CH5, CH7, CH9);
  not not_1 (not_1_out, SC);
  not not_2 (not_2_out, SA);
  not not_3 (not_3_out, SB);
  not not_4 (not_4_out, SA);
  not not_5 (not_5_out, SB);
  not not_6 (not_6_out, SC);
  not not_7 (not_7_out, SA);
  not not_8 (not_8_out, SC);
  not not_9 (not_9_out, SA);
  not not_10 (not_10_out, SB);
  not not_11 (not_11_out, SC);
  not not_12 (not_12_out, SA);
  not not_13 (not_13_out, SA);
  not not_14 (not_14_out, SB);
  not not_15 (not_15_out, SA);
  not not_16 (not_16_out, SB);
  not not_17 (not_17_out, SA);
  not not_18 (not_18_out, SC);
  not not_19 (not_19_out, SB);
  not not_20 (not_20_out, SA);
  and and_1 (and_1_out, not_1_out, not_2_out);
  and and_2 (and_2_out, SC, SA);
  not not_21 (not_21_out, SC);
  and and_3 (and_3_out, not_3_out, not_4_out);
  and and_4 (and_4_out, SB, SA);
  or or_5 (c, not_5_out, SA, SC);
  and and_5 (and_5_out, not_6_out, not_7_out);
  and and_6 (and_6_out, not_8_out, SB);
  and and_7 (and_7_out, SB, not_9_out);
  and and_8 (and_8_out, SC, not_10_out, SA);
  and and_9 (and_9_out, not_11_out, not_12_out);
  and and_10 (and_10_out, SB, not_13_out);
  and and_11 (and_11_out, not_14_out, not_15_out);
  and and_12 (and_12_out, SC, not_16_out);
  and and_13 (and_13_out, SC, not_17_out);
  and and_14 (and_14_out, not_18_out, SB);
  and and_15 (and_15_out, SC, not_19_out);
  and and_16 (and_16_out, SC, not_20_out);
  or or_6 (a, and_1_out, SB, and_2_out, SD);
  or or_7 (b, not_21_out, and_3_out, and_4_out);
  or or_8 (d, and_5_out, and_6_out, and_7_out, and_8_out);
  or or_9 (e, and_9_out, and_10_out);
  or or_10 (f, and_11_out, and_12_out, and_13_out, SD);
  or or_11 (g, and_14_out, and_15_out, and_16_out, SD);
  _7_Segment_Display u_7_segment_display_1 (.g(g), .f(f), .a(a), .b(b), .e(e), .d(d), .c(c));  // open: dp
endmodule
